# Fritzing sketch parts (saved by Fritzing 0.9.3b)
circuit board: 8.46667cm x 5.64444cm

parts:
  U2 = NodeMCU V1.0
  SSD1306 = OLED 128x64 I2C Monochrome Display
  220V_AC_Relay = RELAY-SOLIDSTATE [package=relay-s108t02]
  Relay = Keyes Relay [package=THT]
  7_-_9V_1a = Power plug
  HID_Card_Reader = Header 4 [package=1x04-1mm-ra]
  Part1 = Adafruit ADS1115 16Bit I2C ADC [part_number="Adafruit #1085"]
  SCT013_Curent_Sensor = 3.5mm Audio Jack [package=audio-jack-3.5mm-smd]

nets:
  N1: U2.D1, SSD1306.SCK, Part1.SCL
  N2: U2.D2, SSD1306.SDA, Part1.SDA
  VDD: U2.3V3, SSD1306.VDD, Relay.signal, Part1.VDD
  GND: U2.GND, SSD1306.GND, 220V_AC_Relay.-, Relay.ground, 7_-_9V_1a.GND, HID_Card_Reader.3, Part1.GND
  N3: U2.D5, HID_Card_Reader.2
  N4: U2.D6, HID_Card_Reader.1
  N5: U2.D8, Relay.power
  VIN: U2.Vin, 220V_AC_Relay.+, Relay.NC, Relay.C, Relay.NO, 7_-_9V_1a.VCC, HID_Card_Reader.4
  N6: Part1.AIN1, SCT013_Curent_Sensor.RIGHT
  N7: Part1.AIN0, SCT013_Curent_Sensor.SLEEVE

custom parts:
  NodeMCU V1.0: ESP8266 based NodeMCU
  Keyes Relay: The Keyes 5V relay module is suitable for SCM development, home appliance control. It uses a 5V~12V TIL control signal which can control DC / AC signal.
  Adafruit ADS1115 16Bit I2C ADC: For microcontrollers without an analog-to-digital converter or when you want a higher-precision ADC, the ADS1115 provides 16-bit precision at 860 samples/second over I2C. The chip can be configured as 4 single-ended input channels, or two differential channels. As a nice bonus, it even includes a programmable gain amplifier, up to x16, to help boost up smaller single/differential signals to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
